# Fritzing sketch EEI-Stopwatch (saved by Fritzing 0.9.10b)
breadboards: 1

parts:
  R1 = Resistor [tolerance=±5% power=0.25 resistance=22k package=THT]
  R2 = Resistor [tolerance=±5% power=0.25 resistance=22k package=THT]
  Part1 = Arduino Nano (Rev3.0) (ICSP)
  S3 = SWITCH_SPDT [package=kps-1290]
  BAT2 = 18650 Li-ion battery
  M3 = TP4056 Module [part_number=HW-107]
  M4 = MT3608 Module
  Display1 = 4-Digit 7-segment LED Display [package=THT]
  S4 = Tactile switch 12mm [package=THT]
  S5 = Tactile switch 12mm [package=THT]
  VL53L0X2 = VL53L0X ToF laser distance sensor [package=THT]

nets:
  N1: R1.Pin_0, S4.1, S4.2
  N2: R1.Pin_1, R2.Pin_0, S5.1, S5.2
  N3: R2.Pin_1, Part1.A3
  GND: Part1.GND, M4.pin4, Display1.GND, S4.3, S4.4, S5.3, VL53L0X2.GND
  N4: Part1.D2, Display1.DIO
  N5: Part1.D3, Display1.CLK
  5V: Part1.5V, M4.pin3, Display1.VCC, VL53L0X2.VIN
  N6: Part1.A5, VL53L0X2.SCL
  N7: Part1.A4, VL53L0X2.SDA
  N8: S3.P, M4.pin2
  N9: S3.S, M3.OUT-#4
  N10: BAT2.+, M3.BAT+
  N11: BAT2.-, M3.BAT-
  N12: M3.OUT-#1, M4.pin1

custom parts:
  18650 Li-ion battery: Rechargable 3.7V 18650 Li-ion cell. Based on the work of Kristofer Chan.
  TP4056 Module: TP4056 Lithium Battery Charge Management Module Links: TP4056 website
  MT3608 Module: MT3608 Boost Converter Module Links: Aerosemi MT3608 2A Step Up Converter datasheet
  4-Digit 7-segment LED Display: A 4-digit 7-segments LED display PCB module driven by a TM1637 control IC via 1-wire protocol.
  Tactile switch 12mm: 12 mm tactile switch (push button/momentary switch) from the B3F family.
  Tactile switch 12mm: 12 mm tactile switch (push button/momentary switch) from the B3F family.
  VL53L0X ToF laser distance sensor: Time of Flight laser distance sensor VL53L0X.
